# Fritzing sketch Sketch (saved by Fritzing 0.9.2b)
breadboards: 1

parts:
  Часть1 = Arduino Nano (Rev3.0)
  R1 = Resistor [tolerance=±5% resistance=220 package=THT]
  DHT1 = DHT11 Humitidy and Temperature Sensor
  Nokia_5110_LCD_Module1 = Nokia5110LCDModule

nets:
  GND: Часть1.GND, DHT1.GND, Nokia_5110_LCD_Module1.LED
  N1: Часть1.D3, Nokia_5110_LCD_Module1.Vcc
  N2: Часть1.D4, Nokia_5110_LCD_Module1.Grnd
  N3: Часть1.D5, Nokia_5110_LCD_Module1.SCE
  N4: Часть1.D6, Nokia_5110_LCD_Module1.RST
  N5: Часть1.D7, Nokia_5110_LCD_Module1.D/C
  N6: Часть1.D8, R1.Pin_0, DHT1.DATA
  5V: Часть1.5V, R1.Pin_1, DHT1.VDD
  N7: Часть1.3V3, Nokia_5110_LCD_Module1.6_DN_(MOSI), Nokia_5110_LCD_Module1.SCLK

custom parts:
  DHT11 Humitidy and Temperature Sensor: DHT11 Humidity and Temperature Sensor
  : Nokia 5110 LCD with 8 pin. It's a 45mm*45mm module part. Description: The Nokia 5110 is a basic graphic LCD screen for lots of applications. It was originally intended for as a cell phone screen. This one is mounted on an easy to solder PCB. It uses the PCD8544 controller. The PCD8544 is a low power CMOS LCD controller/driver, designed to drive a graphic display of 48 rows and 84 columns. All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

// code stored in the sketch: DisplayTemp.ino
#include "DHT.h"
#include <SPI.h>
#include <Adafruit_GFX.h>
#include <Adafruit_PCD8544.h>

#define DHTPIN 13


#define NUMFLAKES 10
#define XPOS 0
#define YPOS 1
#define DELTAY 2



// Uncomment whatever type you're using!
#define DHTTYPE DHT11   // DHT 11 
//#define DHTTYPE DHT22   // DHT 22  (AM2302)
//#define DHTTYPE DHT21   // DHT 21 (AM2301)



// Software SPI (slower updates, more flexible pin options):
// pin 6 - Serial clock out (SCLK)
// pin 5 - Serial data out (DIN)
// pin 4 - Data/Command select (D/C)
// pin 3 - LCD chip select (CS)
// pin 2 - LCD reset (RST)
Adafruit_PCD8544 display = Adafruit_PCD8544(7, 6, 5, 4, 3);

DHT dht(DHTPIN, DHTTYPE);
void setup() {
  Serial.begin(9600);
  Serial.print("This shit is going real!");
  dht.begin();
  display.begin();
  display.setContrast(50);
}

void loop() {

  float h = dht.readHumidity();
  float t = dht.readTemperature();
  // check if returns are valid, if they are NaN (not a number) then something went wrong!
  if (isnan(t) || isnan(h) && (t > 0) && (h > 0)) {
    Serial.println("Failed to read from DHT");
  } else {
    Serial.println(t);
    Serial.println(h);

    //display.setTextColor(BLACK);
    display.setTextSize(1);
    delay(200);
    display.clearDisplay();
    display.setCursor(10, 20);
    display.print("Temp: ");
    display.println(t);
    display.setCursor(10, 28);
    display.print("Humid: ");
    display.println(h);
    display.display();

  }
}
